# Fritzing sketch CircuitDiagram (saved by Fritzing 0.9.3b)
breadboards: 1

parts:
  Part1 = Arduino Nano (Rev3.0)
  Part2 = Bluetooth HC-05 Macho
  Part3 = InvenSense MPU6050
  R3 = Resistor [tolerance=±5% resistance=220 package="0402 [SMD]"]
  R1 = Resistor [tolerance=±5% resistance=220 package="0402 [SMD]"]
  R2 = Resistor [tolerance=±5% resistance=220 package="1206 [SMD]"]
  L298N1 = L298N motor driver
  C1 = Capacitor [package=cap-pth-small2]
  C2 = Capacitor [package=cap-pth-small2]
  C3 = Electrolytic Capacitor [capacitance=10μF package="0605 [SMD, electrolytic]"]  # not connected
  M1 = DC Motor
  M2 = DC Motor
  U1 = BATTERY-2 [package=battery-aa]
  U2 = BATTERY-2 [package=battery-aa]

nets:
  N1: Part1.D1/TX, R3.Pin_0
  N2: Part1.D0/RX, Part2.TXD
  GND: Part1.GND, Part2.GND, R2.Pin_1
  N3: Part1.D2, Part3.INT
  N4: Part1.D5, L298N1.connector9, L298N1.connector11
  N5: Part1.D6, L298N1.connector13
  N6: Part1.D7, L298N1.connector14
  N7: Part1.D8, L298N1.connector15
  N8: Part1.D9, L298N1.connector16
  N9: Part1.D10, L298N1.connector10, L298N1.connector12
  N10: Part1.A5, Part3.SCL
  N11: Part1.A4, Part3.SDA
  N12: Part2.RXD, R3.Pin_1
  VCC: Part2.VCC, Part3.VCC
  N13: R1.Pin_0, R2.Pin_0
  N14: L298N1.connector5, U2.+1
  N15: L298N1.connector6, U1.-1
  N16: C1.2, M1.pin_2
  N17: C2.1, M2.pin_1
